# Fritzing sketch MIDI_CV_CONV (saved by Fritzing 0.9.3b)
breadboards: 2

parts:
  パーツ1 = Arduino Pro Mini (5V)  # not connected
  U1 = mystery part, 8 pins [chip_label=TLP552]
  R1 = Resistor [tolerance=±5% resistance=220 package=THT]
  D1 = Rectifier Diode [part_number=1N4001 package="300 mil [THT]"]
  R2 = Resistor [tolerance=±5% resistance=220 package=THT]
  C1 = Ceramic Capacitor [capacitance=100nF package="100 mil [THT, multilayer]"]
  U2 = MIDI_CONN_FEMALE_SUPPORT [package=din_5_female_support]
  U3 = mystery part, 14 pins [chip_label=MCP4922]
  R3 = TRIMPOT [package=trimpot_pth_s3_lock]
  R4 = Resistor [tolerance=±5% resistance=4.7k package=THT]
  R5 = Resistor [tolerance=±5% resistance=220 package=THT]
  R6 = Resistor [tolerance=±5% resistance=220 package=THT]
  U5 = MIDI_CONN_FEMALE_SUPPORT [package=din_5_female_support]
  U4 = mystery part, 20 pins [chip_label=74HC541]
  U6 = mystery part, 16 pins [chip_label=TD62003]
  LED2 = LED - 3mm [color="Green (570nm)" package="3 mm [THT]"]
  LED3 = LED - 3mm [color="Green (570nm)" package="3 mm [THT]"]
  LED4 = LED - 3mm [color="Green (570nm)" package="3 mm [THT]"]
  R7 = Resistor [tolerance=±5% resistance=1k package=THT]
  R8 = Resistor [tolerance=±5% resistance=1k package=THT]
  R9 = Resistor [tolerance=±5% resistance=1k package=THT]
  R10 = Resistor [tolerance=±5% resistance=1k package=THT]
  LED5 = LED - 3mm [color="Green (570nm)" package="3 mm [THT]"]
  C2 = Ceramic Capacitor [capacitance=100nF package="100 mil [THT, multilayer]"]
  C3 = Electrolytic Capacitor [capacitance=1µF package="100 mil [THT, electrolytic]"]
  C4 = Ceramic Capacitor [capacitance=100nF package="100 mil [THT, multilayer]"]
  LED6 = LED - 3mm [color="Green (570nm)" package="3 mm [THT]"]
  LED7 = LED - 3mm [color="Green (570nm)" package="3 mm [THT]"]
  R11 = Resistor [tolerance=±5% resistance=1k package=THT]
  R12 = Resistor [tolerance=±5% resistance=1k package=THT]

nets:
  N1: U1.pin2, R1.Pin_1, D1.cathode
  N2: U1.pin3, D1.anode, U2.MIDI_OUT
  N3: U1.pin5, C1.0
  N4: U1.pin6, R2.Pin_1, U4.pin2
  N5: U1.pin7, U1.pin8, R2.Pin_0, C1.1, U3.pin9
  N6: R1.Pin_0, U2.MIDI_IN
  N7: U3.pin1, R3.CW, R6.Pin_0, U4.pin20, R7.Pin_1, R8.Pin_1, R9.Pin_1, R10.Pin_1, C2.1, C3.+, C4.1, R11.Pin_1, R12.Pin_1
  N8: U3.pin10, U3.pin14
  N9: U3.pin11, U3.pin13, R3.WIPER
  N10: U3.pin12, R4.Pin_1, U5.NC2, U4.pin1, U4.pin3, U4.pin10, U4.pin19, U6.pin1, U6.pin8, C2.0, C3.-, C4.0
  N11: R3.CCW, R4.Pin_0
  N12: R5.Pin_0, U5.MIDI_OUT
  N13: R5.Pin_1, U4.pin18
  N14: R6.Pin_1, U5.MIDI_IN
  N15: U4.pin4, U6.pin2
  N16: U4.pin5, U6.pin3
  N17: U4.pin6, U6.pin4
  N18: U4.pin7, U6.pin5
  N19: U4.pin8, U6.pin6
  N20: U4.pin9, U6.pin7
  N21: U6.pin10, LED7.cathode
  N22: U6.pin11, LED2.cathode
  N23: U6.pin12, LED3.cathode
  N24: U6.pin13, LED4.cathode
  N25: U6.pin14, LED5.cathode
  N26: U6.pin15, LED6.cathode
  N27: LED2.anode, R9.Pin_0
  N28: LED3.anode, R8.Pin_0
  N29: LED4.anode, R7.Pin_0
  N30: R10.Pin_0, LED7.anode
  N31: LED5.anode, R11.Pin_0
  N32: LED6.anode, R12.Pin_0

notes:
  TLP552
  1 NC 8 VCC
  2 IN-A 7 Enable
  3 IN-K 6 VOUT
  4 NC 5 GND
  MCP4922
  1 VDD 14 OUTA
  2 NC 13 VREFA
  3 !CS 12 AVSS
  4 SCK 11 VREFB
  5 SDI 10 OUTB
  6 NC 9 !SHDN
  7 NC 8 LDAC
  GATE 1~6
  MIDI-IN
  MIDI-THRU
  VREF 3.3V
  CV2
  CV1
