# Fritzing sketch MIDI_IN_Test_Arduino_NANO_LPF (saved by Fritzing 0.9.3b)
breadboards: 2

parts:
  C2 = Electrolytic Capacitor [capacitance=1µF package="100 mil [THT, electrolytic]"]
  U4 = mystery part, 8 pins [chip_label=TLP552]
  D2 = Rectifier Diode [part_number=1N4001 package="300 mil [THT]"]
  R3 = Resistor [tolerance=±5% resistance=220 package=THT]
  C3 = Ceramic Capacitor [capacitance=100nF package="100 mil [THT, multilayer]"]
  R4 = Resistor [tolerance=±5% resistance=220 package=THT]
  U5 = MIDI_CONN_FEMALE [package=din_5_female]
  パーツ1 = Arduino Nano (Rev3.0)
  U6 = mystery part, 14 pins [chip_label=MCP4922]
  C4 = Ceramic Capacitor [capacitance=100nF package="100 mil [THT, multilayer]"]
  U7 = LCD-16X2 [package=lcd-8x2]  # not connected
  U8 = mystery part, 4 pins [chip_label="I2C LCD"]
  IC1 = Dual Op-Amp [package=dip08]
  R5 = Resistor [tolerance=±5% resistance=15k package=THT]
  R6 = Resistor [tolerance=±5% resistance=15k package=THT]
  R7 = Resistor [tolerance=±5% resistance=15k package=THT]
  R8 = Resistor [tolerance=±5% resistance=15k package=THT]
  C5 = Film/Foil Capacitor [capacitance=100nF voltage=35V package="5mm [THT, pp]"]
  C6 = Film/Foil Capacitor [capacitance=100nF voltage=35V package="5mm [THT, pp]"]
  C7 = Film/Foil Capacitor [capacitance=100nF voltage=35V package="5mm [THT, pp]"]
  C8 = Ceramic Capacitor [capacitance=100nF package="100 mil [THT, multilayer]"]

nets:
  N1: C2.-, U4.pin5, C3.0, パーツ1.GND, U6.pin12, C4.0, IC1.A_V-, C8.0
  N2: C2.+, U4.pin7, U4.pin8, R3.Pin_0, C3.1, パーツ1.5V, U6.pin1, U6.pin9, C4.1, IC1.A_V+, C6.+, C8.1
  N3: U4.pin2, D2.cathode, R4.Pin_1
  N4: U4.pin3, D2.anode, U5.MIDI_OUT
  N5: U4.pin6, R3.Pin_1, パーツ1.D0/RX
  N6: R4.Pin_0, U5.MIDI_IN
  N7: パーツ1.D9, U6.pin8
  N8: パーツ1.D10, U6.pin3
  N9: パーツ1.D11/MOSI, U6.pin5
  N10: パーツ1.A5, U8.pin3
  N11: パーツ1.A4, U8.pin2
  N12: パーツ1.AREF, U6.pin11, U6.pin13
  N13: パーツ1.D13/SCK, U6.pin4
  N14: U6.pin10, R8.Pin_1
  N15: U6.pin14, R6.Pin_1
  N16: IC1.A_OUT, IC1.A_-IN, C5.-
  N17: IC1.A_+IN, R5.Pin_0, C6.-
  N18: IC1.B_+IN, R7.Pin_0
  N19: IC1.B_-IN, IC1.B_OUT, C7.+
  N20: R5.Pin_1, R6.Pin_0, C5.+
  N21: R7.Pin_1, R8.Pin_0, C7.-

notes:
  TLP552
  1 NC 8 VCC
  2 IN-A 7 Enable
  3 IN-K 6 VOUT
  4 NC 5 GND
  MIDI IN
  TX: MIDI OUT
  RX: MIDI IN
  MCP4922
  1 VDD 14 OUTA
  2 NC 13 VREFA
  3 !CS 12 AVSS
  4 SCK 11 VREFB
  5 SDI 10 OUTB
  6 NC 9 !SHDN
  7 NC 8 LDAC
  CV OUT1
  CV OUT2
  GATE OUT 1~6
