# Fritzing sketch MIDI_IN_Test_Arduino_NANO_RLC_LPF_DFF (saved by Fritzing 0.9.3b)
breadboards: 3

parts:
  C2 = Electrolytic Capacitor [capacitance=1µF package="100 mil [THT, electrolytic]"]
  U4 = mystery part, 8 pins [chip_label=TLP552]
  D2 = Rectifier Diode [part_number=1N4001 package="300 mil [THT]"]
  R3 = Resistor [tolerance=±5% resistance=220 package=THT]
  C3 = Ceramic Capacitor [capacitance=100nF package="100 mil [THT, multilayer]"]
  R4 = Resistor [tolerance=±5% resistance=220 package=THT]
  U5 = MIDI_CONN_FEMALE [package=din_5_female]
  パーツ1 = Arduino Nano (Rev3.0)
  U6 = mystery part, 14 pins [chip_label=MCP4922]
  C4 = Ceramic Capacitor [capacitance=100nF package="100 mil [THT, multilayer]"]
  U7 = LCD-16X2 [package=lcd-8x2]  # not connected
  U8 = mystery part, 4 pins [chip_label="I2C LCD"]
  IC1 = Dual Op-Amp [package=dip08]
  R6 = Resistor [tolerance=±5% resistance=1.5k package=THT]
  R8 = Resistor [tolerance=±5% resistance=1.5k package=THT]
  C6 = Film/Foil Capacitor [capacitance=100nF voltage=35V package="5mm [THT, pp]"]
  C7 = Film/Foil Capacitor [capacitance=100nF voltage=35V package="5mm [THT, pp]"]
  C8 = Ceramic Capacitor [capacitance=100nF package="100 mil [THT, multilayer]"]
  L1 = Inductor [package="400 mil [THT]"]
  L2 = Inductor [package="400 mil [THT]"]
  IC2 = IC, DIP package, 16 pins [chip_label=74HC175]
  C9 = Ceramic Capacitor [capacitance=100nF package="100 mil [THT, multilayer]"]
  IC3 = IC, DIP package, 16 pins [chip_label=TD62003]
  R9 = Resistor [tolerance=±5% resistance=1k package=THT]
  R10 = Resistor [tolerance=±5% resistance=1k package=THT]
  R11 = Resistor [tolerance=±5% resistance=1k package=THT]
  R12 = Resistor [tolerance=±5% resistance=1k package=THT]
  LED1 = LED - 3mm [color="Green (570nm)" package="3 mm [THT]"]
  LED2 = LED - 3mm [color="Green (570nm)" package="3 mm [THT]"]
  LED3 = LED - 3mm [color="Green (570nm)" package="3 mm [THT]"]
  LED4 = LED - 3mm [color="Green (570nm)" package="3 mm [THT]"]
  C10 = Electrolytic Capacitor [capacitance=1µF package="100 mil [THT, electrolytic]"]

nets:
  N1: C2.-, U4.pin5, C3.0, パーツ1.GND, U6.pin12, C4.0, IC1.A_V-, C6.+, C7.-, C8.0, IC2.pin8, C9.0, IC3.pin5, IC3.pin6, IC3.pin7, IC3.pin8, C10.-
  N2: C2.+, U4.pin7, U4.pin8, R3.Pin_0, C3.1, パーツ1.5V, U6.pin1, U6.pin9, C4.1, IC1.A_V+, C8.1, IC2.pin1, IC2.pin16, C9.1, R9.Pin_1, R10.Pin_1, R11.Pin_1, R12.Pin_1, C10.+
  N3: U4.pin2, D2.cathode, R4.Pin_1
  N4: U4.pin3, D2.anode, U5.MIDI_OUT
  N5: U4.pin6, R3.Pin_1, パーツ1.D0/RX
  N6: R4.Pin_0, U5.MIDI_IN
  N7: パーツ1.D2, IC2.pin4
  N8: パーツ1.D3, IC2.pin5
  N9: パーツ1.D4, IC2.pin12
  N10: パーツ1.D5, IC2.pin13
  N11: パーツ1.D9, U6.pin8, IC2.pin9
  N12: パーツ1.D10, U6.pin3
  N13: パーツ1.D11/MOSI, U6.pin5
  N14: パーツ1.A5, U8.pin3
  N15: パーツ1.A4, U8.pin2
  N16: パーツ1.AREF, U6.pin11, U6.pin13
  N17: パーツ1.D13/SCK, U6.pin4
  N18: U6.pin10, R8.Pin_1
  N19: U6.pin14, R6.Pin_1
  N20: IC1.A_OUT, IC1.A_-IN
  N21: IC1.A_+IN, C6.-, L2.pin_0
  N22: IC1.B_+IN, C7.+, L1.pin_0
  N23: IC1.B_-IN, IC1.B_OUT
  N24: R6.Pin_0, L2.pin_1
  N25: R8.Pin_0, L1.pin_1
  N26: IC2.pin2, IC3.pin1
  N27: IC2.pin7, IC3.pin2
  N28: IC2.pin10, IC3.pin3
  N29: IC2.pin15, IC3.pin4
  N30: IC3.pin13, LED4.cathode
  N31: IC3.pin14, LED3.cathode
  N32: IC3.pin15, LED2.cathode
  N33: IC3.pin16, LED1.cathode
  N34: R9.Pin_0, LED1.anode
  N35: R10.Pin_0, LED4.anode
  N36: R11.Pin_0, LED3.anode
  N37: R12.Pin_0, LED2.anode

notes:
  TLP552
  1 NC 8 VCC
  2 IN-A 7 Enable
  3 IN-K 6 VOUT
  4 NC 5 GND
  MIDI IN
  TX: MIDI OUT
  RX: MIDI IN
  MCP4922
  1 VDD 14 OUTA
  2 NC 13 VREFA
  3 !CS 12 AVSS
  4 SCK 11 VREFB
  5 SDI 10 OUTB
  6 NC 9 !SHDN
  7 NC 8 LDAC
  CV OUT1
  CV OUT2
  GATE OUT 1~4
  fc = 1073Hz
  L=100mH
  C=0.22uF
