# Fritzing sketch MIDI_IN_Test_NucleoF303 (saved by Fritzing 0.9.3b)
breadboards: 1

parts:
  C2 = Electrolytic Capacitor [capacitance=1µF package="100 mil [THT, electrolytic]"]
  U3 = mystery part, 30 pins [chip_label=NucleoF303K8]
  U4 = mystery part, 8 pins [chip_label=TLP552]
  D2 = Rectifier Diode [part_number=1N4001 package="300 mil [THT]"]
  R3 = Resistor [tolerance=±5% resistance=220 package=THT]
  C3 = Ceramic Capacitor [capacitance=100nF package="100 mil [THT, multilayer]"]
  R4 = Resistor [tolerance=±5% resistance=220 package=THT]
  U5 = MIDI_CONN_FEMALE [package=din_5_female]

nets:
  N1: C2.-, U3.pin14, U4.pin5, C3.0
  N2: C2.+, U3.pin12, U4.pin7, U4.pin8, R3.Pin_0, C3.1
  N3: U3.pin17, U4.pin6, R3.Pin_1
  N4: U4.pin2, D2.cathode, R4.Pin_1
  N5: U4.pin3, D2.anode, U5.MIDI_OUT
  N6: R4.Pin_0, U5.MIDI_IN

notes:
  TLP552
  1 NC 8 VCC
  2 IN-A 7 Enable
  3 IN-K 6 VOUT
  4 NC 5 GND
  MIDI IN
  D1: MIDI OUT
  D0: MIDI IN
  ※D0とD1の並びが
  逆なので注意
  CV OUT 1~3
  GATE OUT
  1~6
